# Fritzing sketch aligator_fritzing_000 (saved by Fritzing 0.9.2b)
breadboards: 1

parts:
  IC1 = ADS1115 16-bit ADC Breakout
  IC2 = ADS1115 16-bit ADC Breakout
  IC3 = ADS1115 16-bit ADC Breakout
  IC4 = ADS1115 16-bit ADC Breakout
  Part1 = Arduino Nano (Rev3.0)

nets:
  VDD: IC1.VDD, IC2.VDD, IC2.ADDR, IC3.VDD, IC4.VDD, Part1.5V
  GND: IC1.GND, IC1.ADDR, IC2.GND, IC3.GND, IC4.GND, Part1.GND
  N1: IC1.SCL, IC2.SCL, IC3.SCL, IC4.SCL, IC4.ADDR, Part1.A5
  N2: IC1.SDA, IC2.SDA, IC3.SDA, IC3.ADDR, IC4.SDA, Part1.A4

notes:
  0x4B (1001011) ADR -> SCL
  0x4A (1001010) ADR -> SDA
  0x48 (1001000) ADR -> GND
  0x49 (1001001) ADR -> VDD
  ADC Bank 0 - 3
  ADC Bank 12-15
  ADC Bank 8 - 11
  ADC Bank 4 - 7
  ADC Bank 0

custom parts:
  ADS1115 16-bit ADC Breakout: ADS1015 12-bit I2C ADC+PGA Breakout
